# Fritzing sketch Circuit (saved by Fritzing 0.9.3b)
breadboards: 1

parts:
  J1 = Power Jack [package=power_jack_slot]
  U1 = LM2596 step down module
  ESP32_-_Back1 = ESP32 - CAM
  Part1 = Jtron 1 Channel Optoisolated Relay Module [package=relay]
  U2 = LIPO-110mAh [package=lipo-110]
  U3 = SWITCH-SPST-2 [package=r_sw_th]
  U4 = SWITCH-SPST-2 [package=r_sw_th]
  U5 = LIPO-110mAh [package=lipo-110]

nets:
  GND: J1.GND, U1.IN-, U1.OUT-, ESP32_-_Back1.GND, Part1.GND, U2.-, U5.-
  N1: J1.PWR, U3.P
  N2: U1.IN+, Part1.NC, U3.O, U4.O
  N3: U1.OUT+, Part1.VCC
  N4: ESP32_-_Back1.GPIO2, Part1.IN1
  N5: Part1.NO, U2.+
  N6: U4.P, U5.+

notes:
  12v
  5v
  Electronic Lock Door 12v
  LED Module

custom parts:
  LM2596 step down module: LM2596 DC-DC step down power supply module 3 A.
  ESP32 - CAM: The ESP32-CAM has a very competitive small-size camera module that can operate independently as a minimum system with a footprint of only 27*40.5*4.5mm and a deep sleep current of up to 6mA.
